# Fritzing sketch ESP8266_DHT22 (saved by Fritzing 0.9.2b)
circuit board: 8.46667cm x 5.64444cm
stripboards: 1

parts:
  R5 = Resistor [tolerance=±5% resistance=10k package=THT]
  S3 = Pushbutton [package="[THT]"]
  S4 = Pushbutton [package="[THT]"]
  DHT2 = DHT22 Humidity and Temperature Sensor
  J1 = female pin header, 6 pins [form="♀ (female)"]
  R6 = Resistor [tolerance=±5% resistance=10k package=THT]
  U2 = ESP8266 WiFi Module [part_number=ESP8266]
  R7 = Resistor [tolerance=±5% resistance=10k package=THT]

nets:
  VDD: R5.Pin_0, DHT2.VDD, R6.Pin_0, U2.VCC, R7.Pin_0
  N1: R5.Pin_1, S4.Pin_1, S4.Pin_2, U2.RST
  N2: S3.Pin_1, S3.Pin_2, U2.GPIO_0
  GND: S3.Pin_3, S3.Pin_4, S4.Pin_3, S4.Pin_4, DHT2.NULL, DHT2.GND, J1.pin1, U2.GND
  N3: DHT2.DATA, R6.Pin_1, U2.GPIO_2
  N4: J1.pin4, U2.RXD
  N5: J1.pin5, U2.TXD
  N6: U2.CH_PD, R7.Pin_1

custom parts:
  ESP8266 WiFi Module: Generic WiFi Module based on the ESP8266 with onboard PCB antenna and UART communications
